// Logisim project MIPSL.circ as structural Verilog: 13 circuits, main circuit main
module main (
  input  in_1,
  input  in_2,
  output [31:0] ACC,
  output [31:0] ULA,
  output [25:0] \ENDEREÇO_RAM ,
  output [31:0] VALOR_RAM,
  output [31:0] VALOR_ROM
);

  wire clock_1_out, controle_1_en_mon, controle_1_en_pc, controle_1_en_ram, controle_1_en_tec,
       controle_1_rd_ram, controle_1_sel_jump, controle_1_sel_op2, controle_1_sel_ula, controle_1_wr_acc,
       controle_1_wr_ram;
  wire [1:0] controle_1_sel_op1;
  wire [5:0] mipsl_1_go_controle;
  wire [6:0] keyboard_1_data, mipsl_1_din_bus_6_0;
  wire [25:0] mipsl_1_j_im, multiplexer_1_out, n1_1_out_3, pc_1_out_data;
  wire [31:0] ram_1_dout_ram;

  Keyboard keyboard_1 (.clk(clock_1_out), .re(controle_1_en_tec), .clr(in_1), .data(keyboard_1_data));  // open: avail
  RAM ram_1 (
    .ADD_RAM(\ENDEREÇO_RAM ), .CLK(clock_1_out), .EN_RAM(controle_1_en_ram), .WR_RAM(controle_1_wr_ram),
    .RD_RAM(controle_1_rd_ram), .DOUT_RAM(ram_1_dout_ram), .DIN_RAM(VALOR_RAM));
  Clock clock_1 (.out(clock_1_out));
  TTY tty_1 (.data(mipsl_1_din_bus_6_0), .clk(clock_1_out), .we(controle_1_en_mon), .clr(in_2));
  mipsl mipsl_1 (
    .SEL_OP2(controle_1_sel_op2), .GO_CONTROLE(mipsl_1_go_controle), .DOUT_ROM(VALOR_ROM),
    .SEL_OP1(controle_1_sel_op1), .WR_ACC(controle_1_wr_acc), .SEL_ULA(controle_1_sel_ula),
    .ADD_RAM(\ENDEREÇO_RAM ), .DIN_RAM(VALOR_RAM), .CLK(clock_1_out), .DEBUG_ACC(ACC), .DEBUG_ULA(ULA),
    .DOUT_RAM(ram_1_dout_ram), .J_IM(mipsl_1_j_im), .DOUT_TEC(keyboard_1_data),
    .DIN_BUS_6_0(mipsl_1_din_bus_6_0));
  controle controle_1 (
    .SEL_ULA(controle_1_sel_ula), .WR_ACC(controle_1_wr_acc), .EN_RAM(controle_1_en_ram),
    .EN_TEC(controle_1_en_tec), .EN_MON(controle_1_en_mon), .WR_RAM(controle_1_wr_ram),
    .SEL_OP1(controle_1_sel_op1), .SEL_JUMP(controle_1_sel_jump), .RD_RAM(controle_1_rd_ram),
    .EN_PC(controle_1_en_pc), .SEL_OP2(controle_1_sel_op2), .OPCODE(mipsl_1_go_controle));
  PC pc_1 (.DATA(n1_1_out_3), .WR_PC(controle_1_en_pc), .CLK(clock_1_out), .OUT_DATA(pc_1_out_data));
  Multiplexer #(.width(26), .enable("false")) multiplexer_1 (
    .in0(pc_1_out_data), .in1(mipsl_1_j_im), .out(multiplexer_1_out), .sel(controle_1_sel_jump));
  ROM rom_1 (.Address(multiplexer_1_out), .DOUT_ROM(VALOR_ROM));
  _1 u_1_1 (.in_1(pc_1_out_data), .out_3(n1_1_out_3), .plus_1(1'b1));
endmodule

// ULA
module ula (
  input  [31:0] A,
  input  [31:0] B,
  input  SEL_ULA,
  output [31:0] SAIDA
);

  wire [31:0] adder_1_out, subtractor_1_out;

  Adder #(.width(32)) adder_1 (.a(A), .b(B), .out(adder_1_out));  // open: cin, cout
  Multiplexer #(.width(32), .enable("false")) multiplexer_1 (
    .in0(adder_1_out), .in1(subtractor_1_out), .out(SAIDA), .sel(SEL_ULA));
  Subtractor #(.width(32)) subtractor_1 (.a(A), .b(B), .out(subtractor_1_out));  // open: bin, bout
endmodule

module mipsl (
  input  [31:0] DOUT_ROM,
  input  CLK,
  input  [6:0] DOUT_TEC,
  input  [31:0] DOUT_RAM,
  input  [1:0] SEL_OP1,
  input  SEL_OP2,
  input  WR_ACC,
  input  SEL_ULA,
  output [5:0] GO_CONTROLE,
  output [25:0] ADD_RAM,
  output [25:0] J_IM,
  output [31:0] DIN_RAM,
  output [31:0] DEBUG_ACC,
  output [6:0] DIN_BUS_6_0,
  output [31:0] DEBUG_ULA
);

  wire [31:0] extensor2_1_out_2, extensor_1_out_2, ir_1_out_4, multiplexer_1_out, multiplexer_2_out;

  extensor2 extensor2_1 (.in_1(DOUT_TEC), .out_2(extensor2_1_out_2));
  Multiplexer #(.width(32), .enable("false")) multiplexer_1 (
    .in0(DOUT_RAM), .in1(extensor_1_out_2), .out(multiplexer_1_out), .sel(SEL_OP2));
  ula ula_1 (.A(multiplexer_1_out), .B(DEBUG_ACC), .SEL_ULA(SEL_ULA), .SAIDA(DEBUG_ULA));
  IR ir_1 (.DATA(DOUT_ROM), .WR_IR(1'b1), .CLK(CLK), .out_4(ir_1_out_4));
  ACC acc_1 (.DATA(multiplexer_2_out), .WR_ACC(WR_ACC), .CLK(CLK), .out_4(DEBUG_ACC));
  SPLITER spliter_1 (.ENTRADA_IR(ir_1_out_4), .CONTROLE(GO_CONTROLE), .ADD_RAM(ADD_RAM));
  extensor extensor_1 (.in_1(ADD_RAM), .out_2(extensor_1_out_2));
  Multiplexer #(.select(2), .width(32), .enable("false")) multiplexer_2 (
    .in0(DOUT_RAM), .in1(extensor2_1_out_2), .in2(extensor_1_out_2), .in3(DEBUG_ULA),
    .out(multiplexer_2_out), .sel(SEL_OP1));

  assign DIN_BUS_6_0 = DEBUG_ACC[6:0];
  assign DIN_RAM = DEBUG_ACC;
  assign J_IM = ADD_RAM;
endmodule

module ACC (
  input  [31:0] DATA,
  input  WR_ACC,
  input  CLK,
  output [31:0] out_4
);

  Register #(.width(32), .trigger("falling")) register_1 (.D(DATA), .en(WR_ACC), .Q(out_4), .clk(CLK));  // open: clr
endmodule

module IR (
  input  [31:0] DATA,
  input  WR_IR,
  input  CLK,
  output [31:0] out_4
);

  Register #(.width(32)) register_1 (.D(DATA), .en(WR_IR), .Q(out_4), .clk(CLK));  // open: clr
endmodule

// "000000"
module extensor (
  input  [25:0] in_1,
  output [31:0] out_2
);

  assign out_2 = {{6{1'b0}}, in_1};  // Bit_Extender bit_extender_1
endmodule

module SPLITER (
  input  [31:0] ENTRADA_IR,
  output [5:0] CONTROLE,
  output [25:0] ADD_RAM
);


  assign ADD_RAM = ENTRADA_IR[25:0];
  assign CONTROLE = ENTRADA_IR[31:26];
endmodule

module RAM (
  input  [25:0] ADD_RAM,
  input  [31:0] DIN_RAM,
  input  CLK,
  input  EN_RAM,
  input  WR_RAM,
  input  RD_RAM,
  output [31:0] DOUT_RAM
);

  RAM_part #(.addrWidth(24), .dataWidth(32), .bus("separate")) ram_1 (
    .addr(ADD_RAM[23:0]), .din(DIN_RAM), .data(DOUT_RAM), .str(WR_RAM), .sel(EN_RAM), .clk(CLK), .ld(RD_RAM),
    .clr(1'b0));
endmodule

module PC (
  input  [25:0] DATA,
  input  WR_PC,
  input  CLK,
  output [25:0] OUT_DATA
);

  Register #(.width(26)) register_1 (.D(DATA), .en(WR_PC), .Q(OUT_DATA), .clk(CLK));  // open: clr
endmodule

module ROM (
  input  [25:0] Address,
  output [31:0] DOUT_ROM
);

  ROM_part #(.addrWidth(24), .dataWidth(32)) rom_1 (.addr(Address[23:0]), .data(DOUT_ROM), .sel(1'b1));

  // Notes on the sheet:
  //   contents of rom_1 (hex, n*v repeats v):
  //   c000005 4000000 c000003 4000001 10000001 4000002 11800001 14000006 1c000003 4000004 8000002 1c000004
endmodule

module _1 (
  input  [25:0] in_1,
  input  plus_1,
  output [25:0] out_3
);

  wire [25:0] bit_extender_1_out;

  assign bit_extender_1_out = {{25{1'b0}}, plus_1};  // Bit_Extender bit_extender_1
  Adder #(.width(26)) adder_1 (.a(in_1), .b(bit_extender_1_out), .out(out_3));  // open: cin, cout
endmodule

module controle (
  input  [5:0] OPCODE,
  output WR_ACC,
  output EN_RAM,
  output WR_RAM,
  output [1:0] SEL_OP1,
  output RD_RAM,
  output SEL_ULA,
  output EN_PC,
  output EN_TEC,
  output SEL_OP2,
  output EN_MON,
  output SEL_JUMP
);

  wire and_1_out, and_2_out, and_3_out, and_5_out, and_6_out, and_7_out, and_8_out, and_9_out, and_10_out,
       and_11_out, and_12_out, and_13_out, and_14_out, and_15_out, and_16_out, and_17_out, not_1_out,
       not_2_out, not_3_out, not_4_out, not_5_out, not_6_out, not_7_out, not_8_out, not_9_out, not_10_out,
       not_11_out, not_12_out, not_13_out, not_14_out, not_15_out, not_16_out, not_17_out, not_18_out,
       not_19_out, not_20_out, not_21_out, not_22_out, not_23_out, not_24_out, not_25_out, not_26_out,
       not_27_out, not_28_out, not_29_out, not_30_out, not_31_out, not_32_out, not_33_out, not_34_out,
       not_35_out, not_36_out, not_37_out, not_38_out, not_39_out, not_40_out, not_41_out, not_42_out,
       not_43_out, not_44_out, not_45_out, not_46_out, not_47_out, not_48_out, not_49_out, not_50_out,
       not_51_out, not_52_out, not_53_out, not_54_out, not_55_out, not_56_out, not_57_out, not_58_out,
       not_59_out, not_60_out, not_61_out, not_62_out, not_63_out, or_7_out;

  not not_1 (not_1_out, OPCODE[5]);
  not not_2 (not_2_out, OPCODE[4]);
  not not_3 (not_3_out, OPCODE[3]);
  not not_4 (not_4_out, OPCODE[2]);
  not not_5 (not_5_out, OPCODE[1]);
  not not_6 (not_6_out, OPCODE[5]);
  not not_7 (not_7_out, OPCODE[4]);
  not not_8 (not_8_out, OPCODE[3]);
  not not_9 (not_9_out, OPCODE[0]);
  not not_10 (not_10_out, OPCODE[5]);
  not not_11 (not_11_out, OPCODE[4]);
  not not_12 (not_12_out, OPCODE[3]);
  not not_13 (not_13_out, OPCODE[0]);
  not not_14 (not_14_out, OPCODE[5]);
  not not_15 (not_15_out, OPCODE[4]);
  not not_16 (not_16_out, OPCODE[3]);
  not not_17 (not_17_out, OPCODE[2]);
  not not_18 (not_18_out, OPCODE[1]);
  not not_19 (not_19_out, OPCODE[5]);
  not not_20 (not_20_out, OPCODE[4]);
  not not_21 (not_21_out, OPCODE[3]);
  not not_22 (not_22_out, OPCODE[0]);
  not not_23 (not_23_out, OPCODE[5]);
  not not_24 (not_24_out, OPCODE[4]);
  not not_25 (not_25_out, OPCODE[3]);
  not not_26 (not_26_out, OPCODE[0]);
  and and_1 (and_1_out, not_1_out, not_2_out, not_3_out, not_4_out, not_5_out, OPCODE[0]);
  and and_2 (and_2_out, not_6_out, not_7_out, not_8_out, OPCODE[2], not_9_out);
  and and_3 (and_3_out, not_10_out, not_11_out, not_12_out, OPCODE[1], not_13_out);
  and and_4 (WR_RAM, not_14_out, not_15_out, not_16_out, not_17_out, not_18_out, OPCODE[0]);
  and and_5 (and_5_out, not_19_out, not_20_out, not_21_out, OPCODE[2], not_22_out);
  and and_6 (and_6_out, not_23_out, not_24_out, not_25_out, OPCODE[1], not_26_out);
  or or_1 (EN_PC, OPCODE[5], OPCODE[4], OPCODE[3], OPCODE[2], OPCODE[1], OPCODE[0]);
  or or_2 (EN_RAM, and_1_out, and_2_out, and_3_out);
  or or_3 (RD_RAM, and_5_out, and_6_out);
  not not_27 (not_27_out, OPCODE[3]);
  not not_28 (not_28_out, OPCODE[5]);
  not not_29 (not_29_out, OPCODE[4]);
  not not_30 (not_30_out, OPCODE[3]);
  not not_31 (not_31_out, OPCODE[5]);
  not not_32 (not_32_out, OPCODE[4]);
  not not_33 (not_33_out, OPCODE[3]);
  not not_34 (not_34_out, OPCODE[5]);
  not not_35 (not_35_out, OPCODE[4]);
  not not_36 (not_36_out, OPCODE[3]);
  not not_37 (not_37_out, OPCODE[5]);
  not not_38 (not_38_out, OPCODE[4]);
  not not_39 (not_39_out, OPCODE[2]);
  not not_40 (not_40_out, OPCODE[1]);
  not not_41 (not_41_out, OPCODE[5]);
  not not_42 (not_42_out, OPCODE[4]);
  not not_43 (not_43_out, OPCODE[3]);
  not not_44 (not_44_out, OPCODE[2]);
  not not_45 (not_45_out, OPCODE[0]);
  not not_46 (not_46_out, OPCODE[2]);
  not not_47 (not_47_out, OPCODE[1]);
  and and_7 (and_7_out, OPCODE[3], OPCODE[0]);
  and and_8 (and_8_out, OPCODE[1], not_27_out);
  and and_9 (and_9_out, not_28_out, not_29_out, not_30_out, OPCODE[2]);
  and and_10 (and_10_out, not_31_out, not_32_out, not_33_out, OPCODE[1], OPCODE[0]);
  and and_11 (and_11_out, not_34_out, not_35_out, not_36_out, OPCODE[2]);
  and and_12 (and_12_out, not_37_out, not_38_out, OPCODE[3], not_39_out, not_40_out, OPCODE[0]);
  and and_13 (and_13_out, not_41_out, not_42_out, not_43_out);
  and and_14 (and_14_out, not_44_out, not_45_out);
  and and_15 (and_15_out, not_46_out, not_47_out);
  and and_16 (and_16_out, OPCODE[2], OPCODE[0]);
  and and_17 (and_17_out, OPCODE[1], OPCODE[0]);
  or or_4 (WR_ACC, OPCODE[5], OPCODE[4], and_7_out, OPCODE[2], and_8_out);
  or or_5 (SEL_OP1[1], and_9_out, and_10_out);
  or or_6 (SEL_OP1[0], and_11_out, and_12_out);
  or or_7 (or_7_out, and_14_out, and_15_out, and_16_out, and_17_out);
  and and_18 (SEL_OP2, and_13_out, or_7_out);
  not not_48 (not_48_out, OPCODE[5]);
  not not_49 (not_49_out, OPCODE[4]);
  not not_50 (not_50_out, OPCODE[3]);
  not not_51 (not_51_out, OPCODE[5]);
  not not_52 (not_52_out, OPCODE[4]);
  not not_53 (not_53_out, OPCODE[2]);
  not not_54 (not_54_out, OPCODE[1]);
  not not_55 (not_55_out, OPCODE[5]);
  not not_56 (not_56_out, OPCODE[4]);
  not not_57 (not_57_out, OPCODE[2]);
  not not_58 (not_58_out, OPCODE[0]);
  not not_59 (not_59_out, OPCODE[5]);
  not not_60 (not_60_out, OPCODE[4]);
  not not_61 (not_61_out, OPCODE[2]);
  not not_62 (not_62_out, OPCODE[1]);
  not not_63 (not_63_out, OPCODE[0]);
  and and_19 (SEL_ULA, not_48_out, not_49_out, not_50_out, OPCODE[2], OPCODE[1]);
  and and_20 (EN_TEC, not_51_out, not_52_out, OPCODE[3], not_53_out, not_54_out, OPCODE[0]);
  and and_21 (EN_MON, not_55_out, not_56_out, OPCODE[3], not_57_out, OPCODE[1], not_58_out);
  and and_22 (SEL_JUMP, not_59_out, not_60_out, OPCODE[3], not_61_out, not_62_out, not_63_out);
endmodule

module extensor2 (
  input  [6:0] in_1,
  output [31:0] out_2
);

  assign out_2 = {{25{1'b0}}, in_1};  // Bit_Extender bit_extender_1
endmodule
