// Logisim project Lab_1.circ as structural Verilog
module half_adder (
  input  A,
  input  B,
  output S,
  output Cout
);

  xor xor_1 (S, A, B);
  and and_1 (Cout, A, B);
endmodule

module full_adder (
  input  A,
  input  B,
  input  Cin,
  output Sout,
  output Cout
);

  wire half_adder_1_cout, half_adder_1_s, half_adder_2_cout;

  half_adder half_adder_1 (.A(A), .B(B), .S(half_adder_1_s), .Cout(half_adder_1_cout));
  half_adder half_adder_2 (.A(half_adder_1_s), .B(Cin), .S(Sout), .Cout(half_adder_2_cout));
  or or_1 (Cout, half_adder_2_cout, half_adder_1_cout);
endmodule

module full_adder_16 (
  input  [15:0] B,
  input  [15:0] A,
  input  Sub__Cin,
  output Cout,
  output [15:0] Sout
);

  wire full_adder_1_cout, full_adder_2_cout, full_adder_3_cout, full_adder_4_cout, full_adder_5_cout,
       full_adder_6_cout, full_adder_7_cout, full_adder_8_cout, full_adder_9_cout, full_adder_10_cout,
       full_adder_11_cout, full_adder_12_cout, full_adder_13_cout, full_adder_14_cout, full_adder_15_cout,
       xor_1_out, xor_2_out, xor_3_out, xor_4_out, xor_5_out, xor_6_out, xor_7_out, xor_8_out, xor_9_out,
       xor_10_out, xor_11_out, xor_12_out, xor_13_out, xor_14_out, xor_15_out, xor_16_out;

  xor xor_1 (xor_1_out, B[0], Sub__Cin);
  full_adder full_adder_1 (.A(A[0]), .B(xor_1_out), .Cin(Sub__Cin), .Sout(Sout[0]), .Cout(full_adder_1_cout));
  xor xor_2 (xor_2_out, B[2], Sub__Cin);
  xor xor_3 (xor_3_out, B[1], Sub__Cin);
  full_adder full_adder_2 (.A(A[1]), .B(xor_3_out), .Cin(full_adder_1_cout), .Sout(Sout[1]), .Cout(full_adder_2_cout));
  xor xor_4 (xor_4_out, B[3], Sub__Cin);
  full_adder full_adder_3 (.A(A[2]), .B(xor_2_out), .Cin(full_adder_2_cout), .Sout(Sout[2]), .Cout(full_adder_3_cout));
  xor xor_5 (xor_5_out, B[4], Sub__Cin);
  full_adder full_adder_4 (.A(A[4]), .B(xor_5_out), .Cin(full_adder_5_cout), .Sout(Sout[4]), .Cout(full_adder_4_cout));
  full_adder full_adder_5 (.A(A[3]), .B(xor_4_out), .Cin(full_adder_3_cout), .Sout(Sout[3]), .Cout(full_adder_5_cout));
  xor xor_6 (xor_6_out, B[5], Sub__Cin);
  xor xor_7 (xor_7_out, B[6], Sub__Cin);
  full_adder full_adder_6 (.A(A[5]), .B(xor_6_out), .Cin(full_adder_4_cout), .Sout(Sout[5]), .Cout(full_adder_6_cout));
  xor xor_8 (xor_8_out, B[7], Sub__Cin);
  full_adder full_adder_7 (.A(A[6]), .B(xor_7_out), .Cin(full_adder_6_cout), .Sout(Sout[6]), .Cout(full_adder_7_cout));
  xor xor_9 (xor_9_out, B[8], Sub__Cin);
  full_adder full_adder_8 (.A(A[7]), .B(xor_8_out), .Cin(full_adder_7_cout), .Sout(Sout[7]), .Cout(full_adder_8_cout));
  full_adder full_adder_9 (.A(A[8]), .B(xor_9_out), .Cin(full_adder_8_cout), .Sout(Sout[8]), .Cout(full_adder_9_cout));
  xor xor_10 (xor_10_out, B[9], Sub__Cin);
  xor xor_11 (xor_11_out, B[10], Sub__Cin);
  full_adder full_adder_10 (
    .A(A[9]), .B(xor_10_out), .Cin(full_adder_9_cout), .Sout(Sout[9]), .Cout(full_adder_10_cout));
  xor xor_12 (xor_12_out, B[11], Sub__Cin);
  full_adder full_adder_11 (
    .A(A[10]), .B(xor_11_out), .Cin(full_adder_10_cout), .Sout(Sout[10]), .Cout(full_adder_11_cout));
  xor xor_13 (xor_13_out, B[12], Sub__Cin);
  full_adder full_adder_12 (
    .A(A[12]), .B(xor_13_out), .Cin(full_adder_13_cout), .Sout(Sout[12]), .Cout(full_adder_12_cout));
  full_adder full_adder_13 (
    .A(A[11]), .B(xor_12_out), .Cin(full_adder_11_cout), .Sout(Sout[11]), .Cout(full_adder_13_cout));
  xor xor_14 (xor_14_out, B[13], Sub__Cin);
  xor xor_15 (xor_15_out, B[14], Sub__Cin);
  full_adder full_adder_14 (
    .A(A[13]), .B(xor_14_out), .Cin(full_adder_12_cout), .Sout(Sout[13]), .Cout(full_adder_14_cout));
  xor xor_16 (xor_16_out, B[15], Sub__Cin);
  full_adder full_adder_15 (
    .A(A[14]), .B(xor_15_out), .Cin(full_adder_14_cout), .Sout(Sout[14]), .Cout(full_adder_15_cout));
  full_adder full_adder_16 (.A(A[15]), .B(xor_16_out), .Cin(full_adder_15_cout), .Sout(Sout[15]), .Cout(Cout));
endmodule
