// Logisim project Lab_2.circ as structural Verilog
module half_adder (
  input  A,
  input  B,
  output S,
  output Cout
);

  xor xor_1 (S, A, B);
  and and_1 (Cout, A, B);
endmodule

module full_adder (
  input  A,
  input  B,
  input  Cin,
  output Sout,
  output Cout
);

  wire half_adder_1_cout, half_adder_1_s, half_adder_2_cout;

  half_adder half_adder_1 (.A(A), .B(B), .S(half_adder_1_s), .Cout(half_adder_1_cout));
  half_adder half_adder_2 (.A(half_adder_1_s), .B(Cin), .S(Sout), .Cout(half_adder_2_cout));
  or or_1 (Cout, half_adder_2_cout, half_adder_1_cout);
endmodule

module full_adder_16 (
  input  [15:0] B,
  input  [15:0] A,
  input  Sub__Cin,
  output Cout,
  output [15:0] Sout
);

  wire full_adder_1_cout, full_adder_2_cout, full_adder_3_cout, full_adder_4_cout, full_adder_5_cout,
       full_adder_6_cout, full_adder_7_cout, full_adder_8_cout, full_adder_9_cout, full_adder_10_cout,
       full_adder_11_cout, full_adder_12_cout, full_adder_13_cout, full_adder_14_cout, full_adder_15_cout,
       xor_1_out, xor_2_out, xor_3_out, xor_4_out, xor_5_out, xor_6_out, xor_7_out, xor_8_out, xor_9_out,
       xor_10_out, xor_11_out, xor_12_out, xor_13_out, xor_14_out, xor_15_out, xor_16_out;

  xor xor_1 (xor_1_out, B[0], Sub__Cin);
  full_adder full_adder_1 (.A(A[0]), .B(xor_1_out), .Cin(Sub__Cin), .Sout(Sout[0]), .Cout(full_adder_1_cout));
  xor xor_2 (xor_2_out, B[1], Sub__Cin);
  xor xor_3 (xor_3_out, B[2], Sub__Cin);
  full_adder full_adder_2 (.A(A[1]), .B(xor_2_out), .Cin(full_adder_1_cout), .Sout(Sout[1]), .Cout(full_adder_2_cout));
  xor xor_4 (xor_4_out, B[3], Sub__Cin);
  full_adder full_adder_3 (.A(A[2]), .B(xor_3_out), .Cin(full_adder_2_cout), .Sout(Sout[2]), .Cout(full_adder_3_cout));
  xor xor_5 (xor_5_out, B[4], Sub__Cin);
  full_adder full_adder_4 (.A(A[4]), .B(xor_5_out), .Cin(full_adder_5_cout), .Sout(Sout[4]), .Cout(full_adder_4_cout));
  full_adder full_adder_5 (.A(A[3]), .B(xor_4_out), .Cin(full_adder_3_cout), .Sout(Sout[3]), .Cout(full_adder_5_cout));
  xor xor_6 (xor_6_out, B[6], Sub__Cin);
  xor xor_7 (xor_7_out, B[5], Sub__Cin);
  full_adder full_adder_6 (.A(A[5]), .B(xor_7_out), .Cin(full_adder_4_cout), .Sout(Sout[5]), .Cout(full_adder_6_cout));
  xor xor_8 (xor_8_out, B[7], Sub__Cin);
  full_adder full_adder_7 (.A(A[6]), .B(xor_6_out), .Cin(full_adder_6_cout), .Sout(Sout[6]), .Cout(full_adder_7_cout));
  xor xor_9 (xor_9_out, B[8], Sub__Cin);
  full_adder full_adder_8 (.A(A[8]), .B(xor_9_out), .Cin(full_adder_9_cout), .Sout(Sout[8]), .Cout(full_adder_8_cout));
  full_adder full_adder_9 (.A(A[7]), .B(xor_8_out), .Cin(full_adder_7_cout), .Sout(Sout[7]), .Cout(full_adder_9_cout));
  xor xor_10 (xor_10_out, B[10], Sub__Cin);
  xor xor_11 (xor_11_out, B[9], Sub__Cin);
  full_adder full_adder_10 (
    .A(A[9]), .B(xor_11_out), .Cin(full_adder_8_cout), .Sout(Sout[9]), .Cout(full_adder_10_cout));
  xor xor_12 (xor_12_out, B[11], Sub__Cin);
  full_adder full_adder_11 (
    .A(A[10]), .B(xor_10_out), .Cin(full_adder_10_cout), .Sout(Sout[10]), .Cout(full_adder_11_cout));
  xor xor_13 (xor_13_out, B[12], Sub__Cin);
  full_adder full_adder_12 (
    .A(A[11]), .B(xor_12_out), .Cin(full_adder_11_cout), .Sout(Sout[11]), .Cout(full_adder_12_cout));
  full_adder full_adder_13 (
    .A(A[12]), .B(xor_13_out), .Cin(full_adder_12_cout), .Sout(Sout[12]), .Cout(full_adder_13_cout));
  xor xor_14 (xor_14_out, B[14], Sub__Cin);
  xor xor_15 (xor_15_out, B[13], Sub__Cin);
  full_adder full_adder_14 (
    .A(A[13]), .B(xor_15_out), .Cin(full_adder_13_cout), .Sout(Sout[13]), .Cout(full_adder_14_cout));
  xor xor_16 (xor_16_out, B[15], Sub__Cin);
  full_adder full_adder_15 (
    .A(A[14]), .B(xor_14_out), .Cin(full_adder_14_cout), .Sout(Sout[14]), .Cout(full_adder_15_cout));
  full_adder full_adder_16 (.A(A[15]), .B(xor_16_out), .Cin(full_adder_15_cout), .Sout(Sout[15]), .Cout(Cout));
endmodule

module rom_auto (
  input  enable_reg,
  input  clear_reg,
  input  enable_rom,
  input  clk,
  output [7:0] saida_rom
);

  wire [3:0] register_1_q, subtractor_1_out;

  Register #(.width(4)) register_1 (
    .D(subtractor_1_out), .en(enable_reg), .Q(register_1_q), .clk(clk), .clr(clear_reg));
  Subtractor #(.width(4)) subtractor_1 (.a(register_1_q), .b(4'b0001), .out(subtractor_1_out));  // open: bin, bout
  ROM #(.addrWidth(4)) rom_1 (.addr(register_1_q), .data(saida_rom), .sel(enable_rom));

  // Notes on the sheet:
  //   contents of rom_1 (hex, n*v repeats v):
  //   86 c6 d6 76 a1 64 8c ab b3 a9 8d 54 86 c6 d6 76
endmodule

module ram_auto (
  input  load,
  input  select,
  input  store,
  input  nunca_so,
  input  mux_saida,
  input  soma_1,
  input  clk,
  input  [7:0] ram_input,
  input  clear_tudo,
  input  enable_reg_saida,
  output [7:0] saida_ram
);

  wire [3:0] counter_q;
  wire [7:0] multiplexer_1_out, ram_1_data;

  Counter #(.width(4), .max('hf)) counter (
    .load(nunca_so), .count(soma_1), .Q(counter_q), .clk(clk), .clr(clear_tudo));  // open: D, carry
  RAM #(.addrWidth(4), .bus("separate")) ram_1 (
    .addr(counter_q), .din(saida_ram), .data(ram_1_data), .str(store), .sel(select), .clk(clk), .ld(load),
    .clr(clear_tudo));
  Register register_1 (.D(multiplexer_1_out), .en(enable_reg_saida), .Q(saida_ram), .clk(clk), .clr(clear_tudo));
  Multiplexer #(.width(8), .enable("false")) multiplexer_1 (
    .in0(ram_1_data), .in1(ram_input), .out(multiplexer_1_out), .sel(mux_saida));
endmodule

module MAC (
  input  [15:0] A,
  input  [15:0] B,
  input  \Subtração ,
  input  Enable,
  input  Clear,
  output Cout,
  output [15:0] \Saída ,
  output [15:0] out_8,
  output [15:0] \Cout_Multiplicação 
);

  wire CLK_out;
  wire [15:0] multiplier_1_out;

  Multiplier #(.width(16)) multiplier_1 (
    .a(A), .b(B), .out(multiplier_1_out), .cout(\Cout_Multiplicação ));  // open: cin
  Clock CLK (.out(CLK_out));
  Register #(.width(16)) register_1 (.D(\Saída ), .en(Enable), .Q(out_8), .clk(CLK_out), .clr(Clear));
  full_adder_16 full_adder_16_1 (.B(multiplier_1_out), .A(out_8), .Sub__Cin(\Subtração ), .Cout(Cout), .Sout(\Saída ));
endmodule

module MAC_FIR (
  input  enable_rom,
  input  clear_rom,
  input  \Subtração ,
  input  load,
  input  in_5,
  input  select,
  input  store,
  input  nunca_so,
  input  mux_saida,
  input  soma_1,
  input  Enable,
  input  clear_tudo,
  input  enagle_reg_saida,
  input  Clear,
  input  on,
  input  plus_1,
  output [15:0] out_17,
  output [15:0] out_18,
  output Cout,
  output [15:0] \Saída ,
  output [15:0] \Saída_2 ,
  output [15:0] out_22,
  output [15:0] \Cout_Multiplicação ,
  output [7:0] out_24
);

  wire CLK_out;
  wire [7:0] ram_auto_1_saida_ram, register_1_q, rom_auto_1_saida_rom;

  rom_da_ram rom_da_ram_1 (.liga_aq(on), .conta_1(plus_1), .limpa(clear_tudo), .valores_ram(out_24));
  Clock CLK (.out(CLK_out));
  rom_auto rom_auto_1 (
    .enable_reg(enable_rom), .clear_reg(clear_rom), .enable_rom(enable_rom), .clk(CLK_out),
    .saida_rom(rom_auto_1_saida_rom));
  ram_auto ram_auto_1 (
    .load(load), .select(select), .store(store), .nunca_so(nunca_so), .mux_saida(mux_saida), .soma_1(soma_1),
    .clk(CLK_out), .ram_input(out_24), .clear_tudo(clear_tudo), .enable_reg_saida(enagle_reg_saida),
    .saida_ram(ram_auto_1_saida_ram));
  Register register_1 (.D(rom_auto_1_saida_rom), .en(enable_rom), .Q(register_1_q), .clk(CLK_out), .clr(in_5));
  assign out_17 = {{8{1'b0}}, register_1_q};  // Bit_Extender bit_extender_1
  assign out_22 = {{8{1'b0}}, ram_auto_1_saida_ram};  // Bit_Extender bit_extender_2
  Multiplier #(.width(16)) multiplier_1 (
    .a(out_17), .b(out_22), .out(out_18), .cout(\Cout_Multiplicação ));  // open: cin
  full_adder_16 full_adder_16_1 (.B(out_18), .A(\Saída_2 ), .Sub__Cin(\Subtração ), .Cout(Cout), .Sout(\Saída ));
  Register #(.width(16)) register_2 (.D(\Saída ), .en(Enable), .Q(\Saída_2 ), .clk(CLK_out), .clr(Clear));
endmodule

module rom_da_ram (
  input  liga_aq,
  input  conta_1,
  input  limpa,
  output [7:0] valores_ram
);

  wire [3:0] counter_1_q;

  Counter #(.width(4), .max('hf)) counter_1 (
    .count(liga_aq), .Q(counter_1_q), .clk(conta_1), .clr(limpa));  // open: load, D, carry
  ROM #(.addrWidth(4)) rom_1 (.addr(counter_1_q), .data(valores_ram));  // open: sel

  // Notes on the sheet:
  //   contents of rom_1 (hex, n*v repeats v):
  //   54 91 14 4c 60 1c 6 6 63 29 36 64 36 54 5b e
endmodule
